// Logisim project controle.circ as structural Verilog: 1 circuit, main circuit controle
module controle (
  input  [5:0] INSTR_CLASS_5_0,
  input  CLK,
  input  RESET,
  input  DF,
  input  Q_IN,
  input  [3:0] EF_3_0,
  input  D_ZERO,
  output [2:0] NEXT_STATE_2_0,
  output COND_EN,
  output Q_LOAD,
  output DF_LOAD,
  output REG_DEC,
  output REG_INC,
  output IR_LOAD,
  output MEM_WR,
  output MEM_RD,
  output [3:0] REG_SEL_SRC_3_0,
  output [2:0] ADDR_SRC_2_0,
  output [3:0] DST_3_0,
  output [2:0] SRC_B_2_0,
  output [2:0] SRC_A_2_0,
  output [3:0] ALU_OP_3_0,
  output [2:0] ESTADO_OUT_2_0
);

  wire [5:3] undriven;

  // Register #(.width(3)) REG_ESTADO: pin names not known; wires that end beside it: CLK, NEXT_STATE_2_0
  ROM #(.addrWidth(9), .dataWidth(32)) uROM (.addr({INSTR_CLASS_5_0[2:0], undriven, ESTADO_OUT_2_0}));  // open: data
  // Pins of 3 and 6 bits meet at INSTR_CLASS_5_0
  // Pins of 3 and 6 bits meet at {undriven, ESTADO_OUT_2_0}
  // Pins of 1 and 3 bits meet at NEXT_STATE_2_0
endmodule
